# Fritzing sketch OrganScannerBoard (saved by Fritzing 0.9.9b)
stripboards: 7

parts:
  U1 = mystery part, 16 pins [chip_label=CD4021BE]
  U2 = mystery part, 16 pins [chip_label=CD4021BE]
  U3 = mystery part, 16 pins [chip_label=CD4021BE]
  U4 = mystery part, 16 pins [chip_label=CD4021BE]
  U5 = mystery part, 16 pins [chip_label=CD4021BE]
  U6 = mystery part, 16 pins [chip_label=CD4021BE]
  U7 = mystery part, 16 pins [chip_label=CD4021BE]
  U8 = mystery part, 16 pins [chip_label=CD4021BE]
  S1 = Pushbutton [package=THT]
  S2 = Pushbutton [package=THT]
  S3 = Pushbutton [package=THT]
  S4 = Pushbutton [package=THT]  # not connected
  S5 = Pushbutton [package=THT]
  S6 = Pushbutton [package=THT]
  S7 = Pushbutton [package=THT]
  S8 = Pushbutton [package=THT]
  S9 = Pushbutton [package=THT]
  S10 = Pushbutton [package=THT]
  S11 = Pushbutton [package=THT]
  S12 = Pushbutton [package=THT]
  S13 = Pushbutton [package=THT]
  S14 = Pushbutton [package=THT]
  S15 = Pushbutton [package=THT]
  S16 = Pushbutton [package=THT]
  S17 = Pushbutton [package=THT]
  S18 = Pushbutton [package=THT]
  S19 = Pushbutton [package=THT]
  S20 = Pushbutton [package=THT]
  S21 = Pushbutton [package=THT]
  S22 = Pushbutton [package=THT]
  S23 = Pushbutton [package=THT]
  S24 = Pushbutton [package=THT]
  S25 = Pushbutton [package=THT]
  S26 = Pushbutton [package=THT]
  S27 = Pushbutton [package=THT]
  S28 = Pushbutton [package=THT]
  S29 = Pushbutton [package=THT]
  S30 = Pushbutton [package=THT]
  S31 = Pushbutton [package=THT]
  S32 = Pushbutton [package=THT]
  S33 = Pushbutton [package=THT]
  S34 = Pushbutton [package=THT]
  S35 = Pushbutton [package=THT]
  S36 = Pushbutton [package=THT]
  S37 = Pushbutton [package=THT]
  S38 = Pushbutton [package=THT]
  S39 = Pushbutton [package=THT]
  S40 = Pushbutton [package=THT]
  S41 = Pushbutton [package=THT]
  S42 = Pushbutton [package=THT]
  S43 = Pushbutton [package=THT]
  S44 = Pushbutton [package=THT]
  S45 = Pushbutton [package=THT]
  S46 = Pushbutton [package=THT]
  S47 = Pushbutton [package=THT]
  S48 = Pushbutton [package=THT]
  S49 = Pushbutton [package=THT]
  S50 = Pushbutton [package=THT]
  S51 = Pushbutton [package=THT]
  S52 = Pushbutton [package=THT]
  S53 = Pushbutton [package=THT]
  S54 = Pushbutton [package=THT]
  S55 = Pushbutton [package=THT]
  S56 = Pushbutton [package=THT]
  S57 = Pushbutton [package=THT]
  S60 = Pushbutton [package=THT]
  S61 = Pushbutton [package=THT]
  S62 = Pushbutton [package=THT]
  S63 = Pushbutton [package=THT]
  S64 = Pushbutton [package=THT]

nets:
  N1: U1.pin9, U2.pin9, U3.pin9, U4.pin9, U5.pin9, U6.pin9, U7.pin9, U8.pin9
  N2: U1.pin10, U2.pin10, U3.pin10, U4.pin10, U5.pin10, U6.pin10, U7.pin10, U8.pin10
  N3: U1.pin13, S5.leg0
  N4: U1.pin14, S3.leg0
  N5: U1.pin15, S2.leg0
  N6: U1.pin16, U2.pin16, U3.pin16, U4.pin16, U5.pin16, U6.pin16, U7.pin16, U8.pin16
  N7: U2.pin13, S19.leg0
  N8: U2.pin14, S15.leg0
  N9: U2.pin15, S11.leg0
  N10: U3.pin13, S24.leg0
  N11: U3.pin14, S20.leg0
  N12: U3.pin15, S14.leg0
  N13: U4.pin13, S29.leg0
  N14: U4.pin14, S23.leg0
  N15: U4.pin15, S22.leg0
  N16: U5.pin13, S32.leg0
  N17: U5.pin14, S31.leg0
  N18: U5.pin15, S35.leg0
  N19: U6.pin13, S40.leg0
  N20: U6.pin14, S44.leg0
  N21: U6.pin15, S39.leg0
  N22: U7.pin13, S53.leg0
  N23: U7.pin14, S48.leg0
  N24: U7.pin15, S52.leg0
  N25: U8.pin13, S57.leg0
  N26: U8.pin14, S61.leg0
  N27: U8.pin15, S63.leg0
  N28: S1.leg1, S2.leg1, S3.leg1, S5.leg1, S6.leg1, S7.leg1, S8.leg1, S9.leg1, S10.leg1, S11.leg1, S12.leg1, S13.leg1, S14.leg1, S15.leg1, S16.leg1, S17.leg1, S18.leg1, S19.leg1, S20.leg1, S21.leg1, S22.leg1, S23.leg1, S24.leg1, S25.leg1, S26.leg1, S27.leg1, S28.leg1, S29.leg1, S30.leg1, S31.leg1, S32.leg1, S33.leg1, S34.leg1, S35.leg1, S36.leg1, S37.leg1, S38.leg1, S39.leg1, S40.leg1, S41.leg1, S42.leg1, S43.leg1, S44.leg1, S45.leg1, S46.leg1, S47.leg1, S48.leg1, S49.leg1, S50.leg1, S51.leg1, S52.leg1, S53.leg1, S54.leg1, S55.leg1, S56.leg1, S57.leg1, S60.leg1, S61.leg1, S62.leg1, S63.leg1, S64.leg1
